// Logisim project lab12Regfile.circ as structural Verilog: 1 circuit, main circuit main
// CPU
module main (
  input  [1:0] RS,
  input  [1:0] RT,
  input  [1:0] RD,
  input  [7:0] RD_WRITE_VALUE,
  input  RD_WRITE_ENABLE,
  output [7:0] RS_READ_VALUE,
  output [7:0] RT_READ_VALUE,
  output [7:0] REG_0_VALUE,
  output [7:0] REG_1_VALUE,
  output [7:0] REG_2_VALUE,
  output [7:0] REG_3_VALUE
);

  wire clk;

  Clock CLOCK (.out(clk));
endmodule
